// Logisim project Complemento_2.circ as structural Verilog: 4 circuits, main circuit main
module main (
  input  A,
  input  B,
  input  VEM_1,
  input  [3:0] in_4,
  input  [3:0] in_5,
  output VAI_1,
  output S,
  output out_8
);

  wire [3:0] controlled_inverter_4_out;

  ADD1 add1_1 (.S(S), .V(VAI_1), .A(A), .B(B), .C(VEM_1));
  Controlled_Inverter controlled_inverter_1 (.out(controlled_inverter_4_out[3]), .en(in_4[3]));  // open: in
  Controlled_Inverter controlled_inverter_2 (.out(controlled_inverter_4_out[1]), .en(in_4[1]));  // open: in
  Controlled_Inverter controlled_inverter_3 (.out(controlled_inverter_4_out[2]), .en(in_4[2]));  // open: in
  Controlled_Inverter controlled_inverter_4 (.out(controlled_inverter_4_out[0]), .en(in_4[0]));  // open: in
  // ADD4 add4_1: pin names not known; wires that end beside it: out_8, controlled_inverter_4_out, 4'b0001
endmodule

module ADD4 (
  input  [3:0] B,
  input  [3:0] A,
  output OVERFLOW,
  output [3:0] out_4
);

  wire add1_2_v, add1_3_v, add1_4_v;

  // Probe on A
  ADD1 add1_1 (.S(out_4[3]), .V(OVERFLOW), .A(B[3]), .B(A[3]), .C(add1_2_v));
  ADD1 add1_2 (.S(out_4[2]), .V(add1_2_v), .A(A[2]), .B(B[2]), .C(add1_4_v));
  // Probe on out_4
  ADD1 add1_3 (.S(out_4[0]), .V(add1_3_v), .A(A[0]), .B(B[0]), .C(1'b0));
  ADD1 add1_4 (.S(out_4[1]), .V(add1_4_v), .A(A[1]), .B(B[1]), .C(add1_3_v));
  // Probe on B
endmodule

module ADD1 (
  input  A,
  input  B,
  input  C,
  output S,
  output V
);

  wire and_1_out, and_2_out, or_1_out, xor_1_out;

  or or_1 (or_1_out, C, B);
  and and_1 (and_1_out, C, B);
  xor xor_1 (xor_1_out, B, C);
  and and_2 (and_2_out, or_1_out, A);
  xor xor_2 (S, A, xor_1_out);
  or or_2 (V, and_2_out, and_1_out);
endmodule

module complemento2 (
  input  [3:0] in_1,
  output out_2,
  output [3:0] out_3
);

  wire [3:0] not_4_out;

  not not_1 (not_4_out[1], in_1[1]);
  not not_2 (not_4_out[2], in_1[2]);
  not not_3 (not_4_out[3], in_1[3]);
  not not_4 (not_4_out[0], in_1[0]);
  ADD4 add4_1 (.B(4'b0001), .A(not_4_out), .OVERFLOW(out_2), .out_4(out_3));
endmodule
