// Logisim project FLIP FLOP RS.circ as structural Verilog: 2 circuits, main circuit main
module main (
);

  wire clock_1_out;
  wire [3:0] counter_1_q;
  wire [4:0] rom_1_data, shift_register_1_out, shift_register_1_q0, shift_register_1_q1, shift_register_1_q2,
       shift_register_1_q3, shift_register_1_q4, shift_register_1_q5, shift_register_1_q6,
       shift_register_1_q7, shift_register_2_out, shift_register_2_q0, shift_register_2_q1,
       shift_register_2_q2, shift_register_2_q3, shift_register_2_q4, shift_register_2_q5,
       shift_register_2_q6, shift_register_2_q7, shift_register_3_q0, shift_register_3_q1,
       shift_register_3_q2, shift_register_3_q3, shift_register_3_q4, shift_register_3_q5,
       shift_register_3_q6, shift_register_3_q7;

  Counter #(.width(4), .max('hf)) counter_1 (.Q(counter_1_q), .clk(clock_1_out));  // open: load, D, count, carry, clr
  Clock clock_1 (.out(clock_1_out));
  ROM #(.addrWidth(4), .dataWidth(5)) rom_1 (.addr(counter_1_q), .data(rom_1_data));  // open: sel
  Shift_Register #(.width(5)) shift_register_1 (
    .in(rom_1_data), .clk(clock_1_out), .out(shift_register_1_out), .q0(shift_register_1_q0),
    .q1(shift_register_1_q1), .q2(shift_register_1_q2), .q3(shift_register_1_q3), .q4(shift_register_1_q4),
    .q5(shift_register_1_q5), .q6(shift_register_1_q6), .q7(shift_register_1_q7));  // open: shift, load, clr, d0, d1, d2, d3, d4, d5, d6, d7
  DotMatrix #(.matrixcols(8), .matrixrows(5)) dotmatrix_1 (
    .col0(shift_register_1_q0), .col1(shift_register_1_q1), .col2(shift_register_1_q2),
    .col3(shift_register_1_q3), .col4(shift_register_1_q4), .col5(shift_register_1_q5),
    .col6(shift_register_1_q6), .col7(shift_register_1_q7));
  Shift_Register #(.width(5)) shift_register_2 (
    .in(shift_register_1_out), .clk(clock_1_out), .out(shift_register_2_out), .q0(shift_register_2_q0),
    .q1(shift_register_2_q1), .q2(shift_register_2_q2), .q3(shift_register_2_q3), .q4(shift_register_2_q4),
    .q5(shift_register_2_q5), .q6(shift_register_2_q6), .q7(shift_register_2_q7));  // open: shift, load, clr, d0, d1, d2, d3, d4, d5, d6, d7
  DotMatrix #(.matrixcols(8), .matrixrows(5)) dotmatrix_2 (
    .col0(shift_register_2_q0), .col1(shift_register_2_q1), .col2(shift_register_2_q2),
    .col3(shift_register_2_q3), .col4(shift_register_2_q4), .col5(shift_register_2_q5),
    .col6(shift_register_2_q6), .col7(shift_register_2_q7));
  DotMatrix #(.matrixcols(8), .matrixrows(5)) dotmatrix_3 (
    .col0(shift_register_3_q0), .col1(shift_register_3_q1), .col2(shift_register_3_q2),
    .col3(shift_register_3_q3), .col4(shift_register_3_q4), .col5(shift_register_3_q5),
    .col6(shift_register_3_q6), .col7(shift_register_3_q7));
  Shift_Register #(.width(5)) shift_register_3 (
    .in(shift_register_2_out), .clk(clock_1_out), .q0(shift_register_3_q0), .q1(shift_register_3_q1),
    .q2(shift_register_3_q2), .q3(shift_register_3_q3), .q4(shift_register_3_q4), .q5(shift_register_3_q5),
    .q6(shift_register_3_q6), .q7(shift_register_3_q7));  // open: shift, out, load, clr, d0, d1, d2, d3, d4, d5, d6, d7

  // Notes on the sheet:
  //   contents of rom_1 (hex, n*v repeats v):
  //   1f 14 1f 0 11 15 1f 0 1f 11 1f 0 1f 1 1f
endmodule

module Contador (
  input  Clock,
  input  Clear,
  output [4:0] out_3
);

  wire j_k_ff_1_qn, j_k_ff_2_qn, j_k_ff_3_qn, j_k_ff_4_qn;

  J_K_Flip_Flop j_k_ff_1 (
    .J(1'b1), .clk(Clock), .K(1'b1), .Q(out_3[0]), .Qn(j_k_ff_1_qn), .reset(Clear));  // open: preset, en
  J_K_Flip_Flop j_k_ff_2 (
    .J(1'b1), .clk(j_k_ff_1_qn), .K(1'b1), .Q(out_3[1]), .Qn(j_k_ff_2_qn), .reset(Clear));  // open: preset, en
  J_K_Flip_Flop j_k_ff_3 (
    .J(1'b1), .clk(j_k_ff_2_qn), .K(1'b1), .Q(out_3[2]), .Qn(j_k_ff_3_qn), .reset(Clear));  // open: preset, en
  J_K_Flip_Flop j_k_ff_4 (
    .J(1'b1), .clk(j_k_ff_3_qn), .K(1'b1), .Q(out_3[3]), .Qn(j_k_ff_4_qn), .reset(Clear));  // open: preset, en
  J_K_Flip_Flop j_k_ff_5 (.J(1'b1), .clk(j_k_ff_4_qn), .K(1'b1), .Q(out_3[4]), .reset(Clear));  // open: Qn, preset, en

  // Notes on the sheet:
  //   CONTADOR ASSÍNCRONO UP
endmodule
