// Logisim project SIMPLIFICAÇÃO-MACRO.circ as structural Verilog
module \Simplificação_macro  (
  input  A,
  input  B,
  input  C,
  input  D,
  output out_5
);

  wire and_1_out, and_2_out;

  and and_1 (and_1_out, B, D);
  and and_2 (and_2_out, A, ~B, C);  // AND_Gate
  or or_1 (out_5, and_1_out, and_2_out);
endmodule
