// Logisim project mionsimp.circ as structural Verilog: 2 circuits, main circuit main
module main (
  input  A,
  input  B,
  input  C,
  input  D,
  output S
);

  mion mion_1 (.in_1(A), .in_2(B), .in_3(C), .in_4(D), .out_5(S));
endmodule

module mion (
  input  in_1,
  input  in_2,
  input  in_3,
  input  in_4,
  output out_5
);

  wire and_1_out, and_2_out, and_3_out, and_4_out, or_1_out, or_2_out;

  and and_1 (and_1_out, in_3, in_4);
  or or_1 (or_1_out, in_1, in_2);
  and and_2 (and_2_out, in_1, in_2);
  or or_2 (or_2_out, in_3, in_4);
  and and_3 (and_3_out, and_1_out, or_1_out);
  and and_4 (and_4_out, and_2_out, or_2_out);
  or or_3 (out_5, and_3_out, and_4_out);
endmodule
