// Logisim project subtrator.circ as structural Verilog: 5 circuits, main circuit main
module main (
);

  complemento2 complemento2_1 ();  // open: in_1, out_2, out_3
endmodule

module ADD4 (
  input  [3:0] B,
  input  [3:0] A,
  output OVERFLOW,
  output [3:0] out_4
);

  wire add1_2_v, add1_3_v, add1_4_v;

  // Probe on A
  ADD1 add1_1 (.S(out_4[3]), .V(OVERFLOW), .A(B[3]), .B(A[3]), .C(add1_2_v));
  ADD1 add1_2 (.S(out_4[2]), .V(add1_2_v), .A(A[2]), .B(B[2]), .C(add1_4_v));
  // Probe on out_4
  ADD1 add1_3 (.S(out_4[0]), .V(add1_3_v), .A(A[0]), .B(B[0]), .C(1'b0));
  ADD1 add1_4 (.S(out_4[1]), .V(add1_4_v), .A(A[1]), .B(B[1]), .C(add1_3_v));
  // Probe on B
endmodule

module ADD1 (
  input  A,
  input  B,
  input  C,
  output S,
  output V
);

  wire and_1_out, and_2_out, or_1_out, xor_1_out;

  or or_1 (or_1_out, C, B);
  and and_1 (and_1_out, C, B);
  xor xor_1 (xor_1_out, B, C);
  and and_2 (and_2_out, or_1_out, A);
  xor xor_2 (S, A, xor_1_out);
  or or_2 (V, and_2_out, and_1_out);
endmodule

module complemento2 (
  input  [3:0] in_1,
  output out_2,
  output [3:0] out_3
);

  wire [3:0] not_1_out;

  not not_1 (not_1_out[0], in_1[0]);
  not not_2 (not_1_out[1], in_1[1]);
  not not_3 (not_1_out[2], in_1[2]);
  not not_4 (not_1_out[3], in_1[3]);
  ADD4 add4_1 (.B(4'b0001), .A(not_1_out), .OVERFLOW(out_2), .out_4(out_3));
endmodule

module subtrator (
  input  [3:0] in_1,
  input  [3:0] in_2,
  output out_3,
  output [3:0] out_4
);

  wire [3:0] complemento2_1_out_3;

  complemento2 complemento2_1 (.in_1(in_1), .out_3(complemento2_1_out_3));  // open: out_2
  ADD4 add4_1 (.B(complemento2_1_out_3), .A(in_2), .OVERFLOW(out_3), .out_4(out_4));
endmodule
